# Fritzing sketch circuit (saved by Fritzing 0.9.3b)
breadboards: 1

parts:
  Componente1 = Arduino Uno (Rev3) - ICSP
  LCM1602_IIC1 = LCM1602 IIC [part_number="LCM1602 IIC" chip_label="LCM1602 IIC" package="DIP (Dual Inline) [THT]"]
  U1 = LCD-16X2 [package=lcd-16x2_noholes]
  PCB2 = RTC_DS1302_module

nets:
  N1: Componente1.A4/SDA, LCM1602_IIC1.SDA
  N2: Componente1.A5/SCL, LCM1602_IIC1.SCL
  N3: Componente1.D2, PCB2.CLK
  N4: Componente1.D4, PCB2.DAT
  N5: Componente1.D5_PWM, PCB2.RST
  VCC: Componente1.5V, LCM1602_IIC1.VCC, PCB2.VCC
  GND: Componente1.GND, LCM1602_IIC1.GND, PCB2.GND
  VSS: LCM1602_IIC1.VSS, U1.VSS
  VDD: LCM1602_IIC1.VDD, U1.VDD
  N6: LCM1602_IIC1.V0, U1.VO
  N7: LCM1602_IIC1.RS, U1.RS
  N8: LCM1602_IIC1.RW, U1.R_W
  N9: LCM1602_IIC1.E, U1.E
  N10: LCM1602_IIC1.D0, U1.DB0
  N11: LCM1602_IIC1.D1, U1.DB1
  N12: LCM1602_IIC1.D2, U1.DB2
  N13: LCM1602_IIC1.D3, U1.DB3
  N14: LCM1602_IIC1.D4, U1.DB4
  N15: LCM1602_IIC1.D5, U1.DB5
  N16: LCM1602_IIC1.D6, U1.DB6
  N17: LCM1602_IIC1.D7, U1.DB7
  N18: LCM1602_IIC1.A, U1.A
  N19: LCM1602_IIC1.K, U1.K

custom parts:
  LCM1602 IIC: I2C-Module to use a 1602 or 2004 LCD on with the wire.h libory Serial LCD Modul
  RTC_DS1302_module: Arduino module DS1302 SPI Real Time Clock
